# Fritzing sketch maquina_expendedora (saved by Fritzing 1.0.1rc)
breadboards: 1

parts:
  Componente1 = Arduino Uno (Rev3) - ICSP
  LED1 = smd LED [color="Red (633nm)" package="0603 [SMD]"]
  LED2 = smd LED [color="Green (560nm)" package="0603 [SMD]"]
  R1 = Resistor [tolerance=±5% resistance=1k package="0402 [SMD]"]
  U1 = LCD-16X2 [package=lcd-16x2]
  R3 = Rotary Potentiometer (Small) [maximum_resistance=100kΩ knob_status=50% package=THT]
  RHT1 = Humidity and Temperature Sensor RHT03
  R2 = Resistor [tolerance=±5% resistance=1k package="0402 [SMD]"]
  HC-SR04_Sensor_1 = HC-SR04 Ultrasonic Distance Sensor
  R4 = Resistor [tolerance=±5% resistance=1k package="0402 [SMD]"]
  Componente2 = Thumb Joystick
  S1 = Momentary Switch [package=ksa_sealed_tac_switch]

nets:
  N1: Componente1.A2, Componente2.SEL
  N2: Componente1.A3, Componente2.HORZ
  N3: Componente1.A4/SDA, Componente2.VERT
  N4: Componente1.ICSP_MOSI, Componente1.D11_PWM/MOSI, U1.DB5
  GND: Componente1.GND, LED1.cathode, LED2.cathode, U1.VSS, U1.R_W, U1.K, R3.leg2, RHT1.GND_1, HC-SR04_Sensor_1.GND, Componente2.GND, S1.1
  N5: Componente1.D8, U1.RS
  N6: Componente1.D9_PWM, U1.E
  N7: Componente1.D10_PWM/SS, U1.DB4
  N8: Componente1.D12/MISO, U1.DB6
  N9: Componente1.D13/SCK, U1.DB7
  N10: Componente1.D2, R2.Pin_1
  N11: Componente1.D3_PWM, R1.Pin_1
  N12: Componente1.D4, S1.4
  N13: Componente1.D5_PWM, RHT1.Vcc
  N14: Componente1.D6_PWM, HC-SR04_Sensor_1.TRIG
  N15: Componente1.D7, HC-SR04_Sensor_1.ECHO
  VCC: Componente1.5V, U1.VDD, R3.leg1, RHT1.Data-signal, HC-SR04_Sensor_1.VCC, R4.Pin_1, Componente2.VCC
  N16: LED1.anode, R1.Pin_0
  N17: LED2.anode, R2.Pin_0
  N18: U1.VO, R3.wiper
  N19: U1.A, R4.Pin_0
